# Fritzing sketch APRS_AFSK_Test_Circuit (saved by Fritzing 0.9.3b)
breadboards: 1

parts:
  Part1 = Arduino Uno (Rev3)
  SPKR1 = Loudspeaker
  R1 = Resistor [tolerance=±5% resistance=330 package=THT]

nets:
  N1: Part1.D2, R1.Pin_1
  N2: Part1.GND, SPKR1.pin1
  N3: SPKR1.pin2, R1.Pin_0
