# Fritzing sketch APRS_GPS (saved by Fritzing 0.9.3b)
breadboards: 1

parts:
  Part1 = Arduino Uno (Rev3)
  U1 = SUP500F [package=sup500f]
  R1 = Resistor [tolerance=±5% resistance=1k package=THT]
  R2 = Resistor [tolerance=±5% resistance=220 package=THT]
  C1 = Ceramic Capacitor [capacitance=10nF package="100 mil [THT, multilayer]"]
  C2 = Ceramic Capacitor [capacitance=100nF package="100 mil [THT, multilayer]"]
  R3 = Resistor [tolerance=±5% resistance=1k package=THT]
  Q1 = NPN-Transistor [package="TO92 [THT]"]
  R4 = Resistor [tolerance=±5% resistance=220 package=THT]

nets:
  N1: Part1.D8, U1.TX-O
  N2: Part1.D13/SCK, R3.Pin_1
  N3: Part1.D2, R1.Pin_1
  5V: Part1.5V, U1.VCC
  GND: Part1.GND, U1.GND, R2.Pin_0, C1.0, Q1.E
  N4: R1.Pin_0, R2.Pin_1, C1.1, C2.0
  N5: R3.Pin_0, Q1.B
  N6: Q1.C, R4.Pin_1

notes:
  Orange Wire : Radio PTT
  Green Wire : Audio Signal to Radio MIC / AudioIN
  Black Wire ; Radio GND
